# Fritzing sketch skema lampu iot (saved by Fritzing 0.9.3b)

parts:
  U1 = ESP8266 NodeMCU LoLin module
  U2 = 2-Channel 5v Relay Shield [package=relay-2ch5v10a]
  LED1 = LEDs [package=led10mm]
  JACK1 = 2.1mm Barrel Jack with Terminal Block

nets:
  N1: U1.D1, U2.IN1
  GND: U1.GND, U2.GND
  N2: U1.VU, U2.VCC
  N3: U2.K2-In, JACK1.POS
  N4: U2.K2-On, LED1.C
  N5: LED1.A, JACK1.NEG

custom parts:
  ESP8266 NodeMCU LoLin module: ESP8266 based NodeMCU
  2-Channel 5v Relay Shield: 2 Channel 5v Relay Shield w. 2x SPD-06VDC-SD-C
  LEDs: LEDs Standard schematic elements and footprints for 5mm, 3mm, 1206, and 0603 sized LEDs. 5mm - Spark Fun Electronics SKU : COM-00529 (and others)
